# Fritzing sketch ArduinoX2_SoftwareSerial_wire (saved by Fritzing 0.9.3b)

parts:
  元件1 = Arduino Uno (Rev3)
  元件2 = Arduino Uno (Rev3)

nets:
  N1: 元件1.D10_PWM/SS, 元件2.D11_PWM/MOSI
  N2: 元件1.D11_PWM/MOSI, 元件2.D10_PWM/SS
  GND: 元件1.GND, 元件2.GND

notes:
  使用SoftwareSerial定義 D10為RX , D11為TX，兩個Arduino對連，RX接對方TX，TX接對方RX，GND接對方GND(共地)，可以在沒藍牙模組時，用有線方式開發程式，到時設定好藍牙模組，接上立即可用，可以随時上傳程式，不用拆接線
