# Fritzing sketch ArduinoX2_wire (saved by Fritzing 0.9.3b)

parts:
  元件1 = Arduino Uno (Rev3)
  元件2 = Arduino Uno (Rev3)

nets:
  GND: 元件1.GND, 元件2.GND
  N1: 元件1.D0/RX, 元件2.D1/TX
  N2: 元件1.D1/TX, 元件2.D0/RX

notes:
  兩個Arduino對連，RX接對方TX，TX接對方RX，GND接對方GND(共地)，可以在沒藍牙模組時，用有線方式開發程式，到時設定好藍牙模組，接上立即可用 Serial.read Serial.write 互傳資訊，上傳程式時，要將此線移除，上傳完成再接上
