# Fritzing sketch HC-05_AT_mode (saved by Fritzing 0.9.3b)
breadboards: 1

parts:
  元件1 = Arduino Uno (Rev3)
  元件2 = Bluetooth HC-05 Macho

nets:
  N1: 元件1.D10_PWM/SS, 元件2.TXD
  N2: 元件1.D11_PWM/MOSI, 元件2.RXD
  GND: 元件1.GND, 元件2.GND
  5V: 元件1.5V, 元件2.VCC

notes:
  Key 線拉好，不接上
  Key 接5V
