# Fritzing sketch HC-05_Master_Slave_SoftwareSerial (saved by Fritzing 0.9.3b)
breadboards: 1

parts:
  元件1 = Arduino Uno (Rev3)
  元件2 = Bluetooth HC-05 Macho
  S1 = Momentary Switch [package=ksa_sealed_tac_switch]
  R1 = Resistor [tolerance=±5% resistance=1k package=THT]

nets:
  N1: 元件1.D10_PWM/SS, 元件2.TXD
  N2: 元件1.D11_PWM/MOSI, 元件2.RXD
  GND: 元件1.GND, 元件2.GND, R1.Pin_0
  N3: 元件1.D2, S1.3
  5V: 元件1.5V, 元件2.VCC, S1.1
  N4: S1.4, R1.Pin_1

notes:
  Key pin 不用接
